// Logisim project expressoeslogicas_a_b.circ as structural Verilog: 2 circuits, main circuit ITEM_B_a295c9e3
module ITEM_B_a295c9e3 (
  input  A,
  input  B,
  input  C,
  input  D,
  output X
);

  wire and_1_out, and_2_out, not_1_out, not_2_out;

  not not_1 (not_1_out, B);
  not not_2 (not_2_out, C);
  and and_1 (and_1_out, not_1_out, not_2_out);
  and and_2 (and_2_out, A, not_1_out, D);
  or or_1 (X, and_1_out, and_2_out);

  // Notes on the sheet:
  //   X = ~B⋅~C+A⋅~B⋅D
endmodule

module ITEM_A_473c044a (
  input  A,
  input  B,
  input  C,
  output X
);

  wire not_1_out, or_1_out;

  or or_1 (or_1_out, ~A, ~B);  // OR_Gate
  not not_1 (not_1_out, or_1_out);
  and and_1 (X, not_1_out, B, C);

  // Notes on the sheet:
  //   X = A⋅B⋅C
endmodule
