// Logisim project questao_03.circ as structural Verilog: 1 circuit, main circuit main
module main (
  input  A,
  input  B,
  input  C,
  input  D,
  output Y
);

  wire and_1_out, and_2_out, and_3_out, not_1_out, not_2_out, not_3_out, not_4_out, not_5_out;

  not not_1 (not_1_out, A);
  and and_1 (and_1_out, not_1_out, not_2_out);
  not not_2 (not_2_out, B);
  not not_3 (not_3_out, B);
  and and_2 (and_2_out, not_3_out, not_4_out);
  not not_4 (not_4_out, D);
  and and_3 (and_3_out, A, C, not_5_out);
  not not_5 (not_5_out, D);
  or or_1 (Y, and_1_out, and_2_out, and_3_out);

  // Notes on the sheet:
  //   Y = ~A⋅~B+~B⋅~D+A⋅C⋅~D
endmodule
