// Logisim project questao_04.circ as structural Verilog: 1 circuit, main circuit main
module main (
  input  H,
  input  U,
  input  T,
  input  F,
  output A
);

  wire and_1_out, and_2_out;

  and and_1 (and_1_out, U, F);
  and and_2 (and_2_out, H, T);
  or or_1 (A, and_1_out, and_2_out);

  // Notes on the sheet:
  //   A = U⋅F+H⋅T
endmodule
