// Logisim project questao_05.circ as structural Verilog: 1 circuit, main circuit main
module main (
  input  B0,
  input  B1,
  input  B2,
  output Y3,
  output Y2,
  output Y1,
  output Y0
);

  wire and_3_out, and_4_out, and_5_out, not_1_out, not_2_out, not_3_out, not_4_out;

  and and_1 (Y3, B0, B1);
  not not_1 (not_1_out, B1);
  not not_2 (not_2_out, B0);
  not not_3 (not_3_out, B1);
  not not_4 (not_4_out, B2);
  and and_2 (Y2, B0, not_1_out);
  and and_3 (and_3_out, not_2_out, not_3_out, not_4_out);
  and and_4 (and_4_out, B1, B2);
  and and_5 (and_5_out, B0, B2);
  or or_1 (Y1, and_3_out, and_4_out, and_5_out);

  assign Y0 = 1'b1;

  // Notes on the sheet:
  //   Y3 = B0⋅B1
  //   Y2 = B0⋅~B1
  //   Y1 = ~B0⋅~B1⋅~B2+B1⋅B2+B0⋅B2
  //   Y0 = 1
endmodule
